// Logisim project 16-bit.circ as structural Verilog: 1 circuit, main circuit main
module main (
  input  in_1,
  input  in_2,
  input  in_3,
  input  [15:0] in_4,
  input  [15:0] in_5,
  output [15:0] out_6
);

  wire not_1_out;
  wire [15:0] n1_bit_alu_1_out_6, shift_1_x2;

  shift shift_1 (.in_1(in_4), .in_2(in_5), .X2(shift_1_x2), .in_3(in_1), .in_4(in_2), .in_5(in_3));
  _1_bit_ALU u_1_bit_alu_1 (
    .in_2(in_4[0]), .in_1(in_5[0]), .out_6(n1_bit_alu_1_out_6[0]), .in_5(in_3), .in_4(in_2), .in_3(in_1));
  _1_bit_ALU u_1_bit_alu_2 (
    .in_2(in_4[1]), .in_1(in_5[1]), .out_6(n1_bit_alu_1_out_6[1]), .in_5(in_3), .in_4(in_2), .in_3(in_1));
  _1_bit_ALU u_1_bit_alu_3 (
    .in_2(in_4[2]), .in_1(in_5[2]), .out_6(n1_bit_alu_1_out_6[2]), .in_5(in_3), .in_4(in_2), .in_3(in_1));
  _1_bit_ALU u_1_bit_alu_4 (
    .in_2(in_4[3]), .in_1(in_5[3]), .out_6(n1_bit_alu_1_out_6[3]), .in_5(in_3), .in_4(in_2), .in_3(in_1));
  _1_bit_ALU u_1_bit_alu_5 (
    .in_2(in_4[4]), .in_1(in_5[4]), .out_6(n1_bit_alu_1_out_6[4]), .in_5(in_3), .in_4(in_2), .in_3(in_1));
  _1_bit_ALU u_1_bit_alu_6 (
    .in_2(in_4[5]), .in_1(in_5[5]), .out_6(n1_bit_alu_1_out_6[5]), .in_5(in_3), .in_4(in_2), .in_3(in_1));
  _1_bit_ALU u_1_bit_alu_7 (
    .in_2(in_4[6]), .in_1(in_5[6]), .out_6(n1_bit_alu_1_out_6[6]), .in_5(in_3), .in_4(in_2), .in_3(in_1));
  _1_bit_ALU u_1_bit_alu_8 (
    .in_2(in_4[7]), .in_1(in_5[7]), .out_6(n1_bit_alu_1_out_6[7]), .in_5(in_3), .in_4(in_2), .in_3(in_1));
  _1_bit_ALU u_1_bit_alu_9 (
    .in_2(in_4[8]), .in_1(in_5[8]), .out_6(n1_bit_alu_1_out_6[8]), .in_5(in_3), .in_4(in_2), .in_3(in_1));
  _1_bit_ALU u_1_bit_alu_10 (
    .in_2(in_4[9]), .in_1(in_5[9]), .out_6(n1_bit_alu_1_out_6[9]), .in_5(in_3), .in_4(in_2), .in_3(in_1));
  _1_bit_ALU u_1_bit_alu_11 (
    .in_2(in_4[10]), .in_1(in_5[10]), .out_6(n1_bit_alu_1_out_6[10]), .in_5(in_3), .in_4(in_2), .in_3(in_1));
  _1_bit_ALU u_1_bit_alu_12 (
    .in_2(in_4[11]), .in_1(in_5[11]), .out_6(n1_bit_alu_1_out_6[11]), .in_5(in_3), .in_4(in_2), .in_3(in_1));
  _1_bit_ALU u_1_bit_alu_13 (
    .in_2(in_4[12]), .in_1(in_5[12]), .out_6(n1_bit_alu_1_out_6[12]), .in_5(in_3), .in_4(in_2), .in_3(in_1));
  _1_bit_ALU u_1_bit_alu_14 (
    .in_2(in_4[13]), .in_1(in_5[13]), .out_6(n1_bit_alu_1_out_6[13]), .in_5(in_3), .in_4(in_2), .in_3(in_1));
  _1_bit_ALU u_1_bit_alu_15 (
    .in_2(in_4[14]), .in_1(in_5[14]), .out_6(n1_bit_alu_1_out_6[14]), .in_5(in_3), .in_4(in_2), .in_3(in_1));
  _1_bit_ALU u_1_bit_alu_16 (
    .in_2(in_4[15]), .in_1(in_5[15]), .out_6(n1_bit_alu_1_out_6[15]), .in_5(in_3), .in_4(in_2), .in_3(in_1));
  not not_1 (not_1_out, in_1);
  assign out_6 = in_1 ? shift_1_x2 : 16'bz;  // Controlled_Buffer controlled_buffer_1
  assign out_6 = not_1_out ? n1_bit_alu_1_out_6 : 16'bz;  // Controlled_Buffer controlled_buffer_2
endmodule
