// Logisim project ALU.circ as structural Verilog: 1 circuit, main circuit 1 bit ALU
module _1_bit_ALU (
  input  in_1,
  input  in_2,
  input  in_3,
  input  in_4,
  input  in_5,
  output out_6
);

  wire and_1_out, nor_1_out, or_1_out, xor_1_out;

  and and_1 (and_1_out, in_1, in_2);
  or or_1 (or_1_out, in_1, in_2);
  nor nor_1 (nor_1_out, in_1, in_2);
  xor xor_1 (xor_1_out, in_1, in_2);
  Multiplexer #(.select(3)) multiplexer_1 (
    .in0(and_1_out), .in1(or_1_out), .in2(nor_1_out), .in3(xor_1_out), .out(out_6), .sel({in_3, in_4, in_5}));  // open: in4, in5, in6, in7, en
endmodule
