// Logisim project Alu 1000.circ as structural Verilog: 1 circuit, main circuit Alu 0001
module Alu_0001 (
  input  [15:0] in_1,
  input  [15:0] in_2,
  input  in_3,
  input  in_4,
  input  in_5,
  output [15:0] out_6,
  output out_7,
  output out_8
);

  wire comparator_1_lt, comparator_2_lt, comparator_3_eq, decoder_1_out0, decoder_1_out1, decoder_1_out2,
       decoder_1_out3, decoder_1_out4, decoder_1_out5;
  wire [15:0] adder_1_out, bit_extender_1_out, bit_extender_2_out, bit_extender_3_out, or_1_out, or_2_out,
       subtractor_1_out;

  Decoder #(.select(3)) decoder_1 (
    .out0(decoder_1_out0), .out1(decoder_1_out1), .out2(decoder_1_out2), .out3(decoder_1_out3),
    .out4(decoder_1_out4), .out5(decoder_1_out5), .out6(out_7), .out7(out_8), .sel({in_3, in_4, in_5}));  // open: en
  Comparator #(.width(16)) comparator_1 (.a(in_1), .b(in_2), .lt(comparator_1_lt));  // open: gt, eq
  Comparator #(.width(16), .mode("unsigned")) comparator_2 (.a(in_1), .b(in_2), .lt(comparator_2_lt));  // open: gt, eq
  Comparator #(.width(16)) comparator_3 (.a(in_2), .b(in_1), .eq(comparator_3_eq));  // open: gt, lt
  assign bit_extender_1_out = {{15{1'b0}}, comparator_1_lt};  // Bit_Extender bit_extender_1
  assign bit_extender_2_out = {{15{1'b0}}, comparator_2_lt};  // Bit_Extender bit_extender_2
  assign bit_extender_3_out = {{15{1'b0}}, comparator_3_eq};  // Bit_Extender bit_extender_3
  Adder #(.width(16)) adder_1 (.a(in_1), .b(in_2), .out(adder_1_out));  // open: cin, cout
  Subtractor #(.width(16)) subtractor_1 (.a(in_1), .b(in_2), .out(subtractor_1_out));  // open: bin, bout
  assign or_1_out = bit_extender_1_out | bit_extender_3_out;  // OR_Gate or_1, 16 bits wide
  assign or_2_out = bit_extender_2_out | bit_extender_3_out;  // OR_Gate or_2, 16 bits wide
  assign out_6 = decoder_1_out0 ? adder_1_out : 16'bz;  // Controlled_Buffer controlled_buffer_1
  assign out_6 = decoder_1_out1 ? subtractor_1_out : 16'bz;  // Controlled_Buffer controlled_buffer_2
  assign out_6 = decoder_1_out2 ? bit_extender_1_out : 16'bz;  // Controlled_Buffer controlled_buffer_3
  assign out_6 = decoder_1_out3 ? bit_extender_2_out : 16'bz;  // Controlled_Buffer controlled_buffer_4
  assign out_6 = decoder_1_out4 ? or_1_out : 16'bz;  // Controlled_Buffer controlled_buffer_5
  assign out_6 = decoder_1_out5 ? or_2_out : 16'bz;  // Controlled_Buffer controlled_buffer_6

  // Notes on the sheet:
  //   in_3: pull=up
endmodule
