// Logisim project Branch.circ as structural Verilog: 1 circuit, main circuit main
module main (
  input  [15:0] in_1,
  input  [15:0] in_2,
  output Zero_flag,
  output BEQ,
  output BLT,
  output BGT,
  output BGTZ,
  output BLTZ,
  output BGEZ,
  output BLEZ
);

  wire comparator_2_eq;

  Comparator #(.width(16)) comparator_1 (.a(in_1), .b(in_2), .gt(BGT), .eq(Zero_flag), .lt(BLT));
  Comparator #(.width(16)) comparator_2 (.a(in_1), .b({16{1'b0}}), .gt(BGTZ), .eq(comparator_2_eq), .lt(BLTZ));
  not not_1 (BEQ, Zero_flag);
  or or_1 (BGEZ, BGTZ, comparator_2_eq);
  or or_2 (BLEZ, comparator_2_eq, BLTZ);

  // Notes on the sheet:
  //   Zero_flag: pull=up
  //   BEQ: pull=up
endmodule
