// Logisim project CU(3)(1).circ as structural Verilog
module Control_Unit (
  input  op1,
  input  op2,
  input  op3,
  input  op4,
  output RegDis,
  output RegWr,
  output Extop,
  output AluSrc,
  output MemRd,
  output MemWr,
  output MemToReg,
  output Jump,
  output Branch
);

  wire and_1_out, and_2_out, and_3_out, and_4_out, and_5_out, and_6_out, and_7_out, and_8_out, and_9_out,
       and_10_out, and_11_out, and_12_out, and_13_out, and_15_out, and_16_out, not_1_out, not_2_out,
       not_3_out, not_4_out, not_5_out, not_6_out, not_7_out, not_8_out, not_9_out, not_10_out, not_11_out,
       not_12_out, not_13_out, not_14_out, not_15_out, not_16_out, not_17_out, not_18_out, not_19_out,
       not_20_out, not_21_out, not_22_out, not_23_out, not_24_out, not_25_out, not_26_out;

  not not_1 (not_1_out, op1);
  and and_1 (and_1_out, not_1_out, not_2_out);
  not not_2 (not_2_out, op3);
  and and_2 (and_2_out, op1, op3, op4);
  not not_3 (not_3_out, op1);
  not not_4 (not_4_out, op2);
  and and_3 (and_3_out, not_3_out, not_4_out, not_5_out);
  not not_5 (not_5_out, op3);
  not not_6 (not_6_out, op2);
  and and_4 (and_4_out, not_6_out, not_7_out);
  not not_7 (not_7_out, op4);
  not not_8 (not_8_out, op1);
  and and_5 (and_5_out, not_8_out, op2, op3);
  not not_9 (not_9_out, op2);
  and and_6 (and_6_out, op1, not_9_out, op3);
  not not_10 (not_10_out, op2);
  and and_7 (and_7_out, not_10_out, not_11_out);
  not not_11 (not_11_out, op4);
  not not_12 (not_12_out, op2);
  and and_8 (and_8_out, not_12_out, op3);
  and and_9 (and_9_out, op2, not_13_out);
  not not_13 (not_13_out, op3);
  not not_14 (not_14_out, op1);
  and and_10 (and_10_out, not_14_out, op3);
  not not_15 (not_15_out, op2);
  and and_11 (and_11_out, op1, not_15_out, not_16_out);
  not not_16 (not_16_out, op4);
  not not_17 (not_17_out, op1);
  not not_18 (not_18_out, op2);
  not not_19 (not_19_out, op4);
  not not_20 (not_20_out, op1);
  not not_21 (not_21_out, op2);
  not not_22 (not_22_out, op1);
  not not_23 (not_23_out, op2);
  and and_12 (and_12_out, not_22_out, not_23_out, op3);
  not not_24 (not_24_out, op2);
  and and_13 (and_13_out, not_24_out, op3, op4);
  not not_25 (not_25_out, op2);
  and and_14 (Jump, op1, not_25_out, op4);
  and and_15 (and_15_out, op2, not_26_out);
  not not_26 (not_26_out, op3);
  and and_16 (and_16_out, op1, op2);
  or or_1 (RegDis, and_1_out, and_2_out);
  or or_2 (RegWr, and_3_out, and_4_out, and_5_out, and_6_out);
  or or_3 (Extop, and_7_out, and_8_out, and_9_out, op1);
  or or_4 (AluSrc, and_10_out, and_11_out);
  and and_17 (MemRd, not_17_out, not_18_out, op3, not_19_out);
  and and_18 (MemWr, not_20_out, not_21_out, op3, op4);
  or or_5 (MemToReg, and_12_out, and_13_out);
  or or_6 (Branch, and_15_out, and_16_out);
endmodule
