// Logisim project I-Type.circ as structural Verilog: 1 circuit, main circuit I-Type
module I_Type (
  input  [15:0] in_1,
  input  [15:0] in_2,
  input  in_3,
  input  in_4,
  input  in_5,
  input  in_6,
  output [15:0] out_7
);

  wire decoder_1_out6, decoder_1_out7, decoder_1_out8;
  wire [15:0] adder_1_out, and_1_out, or_1_out;

  Decoder #(.select(4)) decoder_1 (
    .out6(decoder_1_out6), .out7(decoder_1_out7), .out8(decoder_1_out8), .sel({in_3, in_4, in_5, in_6}));  // open: out0, out1, out2, out3, out4, out5, out9, out10, out11, out12, out13, out14, out15, en
  Adder #(.width(16)) adder_1 (.a(in_1), .b(in_2), .out(adder_1_out));  // open: cin, cout
  assign and_1_out = in_1 & in_2;  // AND_Gate and_1, 16 bits wide
  assign or_1_out = in_1 | in_2;  // OR_Gate or_1, 16 bits wide
  assign out_7 = decoder_1_out6 ? and_1_out : 16'bz;  // Controlled_Buffer controlled_buffer_1
  assign out_7 = decoder_1_out7 ? or_1_out : 16'bz;  // Controlled_Buffer controlled_buffer_2
  assign out_7 = decoder_1_out8 ? adder_1_out : 16'bz;  // Controlled_Buffer controlled_buffer_3
endmodule
