// Logisim project Pipeline_CPU.circ as structural Verilog: 4 circuits, main circuit IF/ID
module IF_ID (
  input  clk,
  input  clr,
  input  [15:0] InstIF,
  input  [15:0] PCPlus4ID,
  input  En,
  output [15:0] InstID,
  output [15:0] PCPlus4IF
);

  Register #(.width(16)) register_1 (.D(InstIF), .en(En), .Q(InstID), .clk(clk), .clr(clr));
  Register #(.width(16)) register_2 (.D(PCPlus4ID), .en(En), .Q(PCPlus4IF), .clk(clk), .clr(clr));
endmodule

module ID_EX (
  input  clk,
  input  clr,
  input  BranchID,
  input  [11:0] ImmID,
  input  RegrtLID,
  input  [2:0] RsAdd,
  input  RegWrID,
  input  [15:0] R1ID,
  input  [2:0] RtAdd,
  input  ExtOPID,
  input  ALUSRCID,
  input  [15:0] R2ID,
  input  [15:0] JumpAdd,
  input  MemReadID,
  input  [15:0] PCPlus4ID,
  input  MemWriteID,
  input  [2:0] RdID,
  input  MemoryToRegID,
  input  jID,
  input  En,
  output BranchEX,
  output [11:0] ImmEX,
  output RegrtLEX,
  output [2:0] RsAddEx,
  output RegWrEX,
  output [15:0] R1EX,
  output [2:0] RtAddEx,
  output ExtOPEX,
  output ALUSRCEX,
  output [15:0] R2EX,
  output [15:0] JumpAddEx,
  output MemReadEX,
  output [15:0] PCPlusEX,
  output MemWriteEX,
  output [2:0] RdEX,
  output MemoryToRegEX,
  output jEX
);

  Register #(.width(12)) register_1 (.D(ImmID), .en(En), .Q(ImmEX), .clk(clk), .clr(clr));
  Register #(.width(16)) register_2 (.D(R1ID), .en(En), .Q(R1EX), .clk(clk), .clr(clr));
  Register #(.width(16)) register_3 (.D(R2ID), .en(En), .Q(R2EX), .clk(clk), .clr(clr));
  Register #(.width(3)) register_4 (.D(RdID), .en(En), .Q(RdEX), .clk(clk), .clr(clr));
  Register #(.width(3)) register_5 (.D(RsAdd), .en(En), .Q(RsAddEx), .clk(clk), .clr(clr));
  Register #(.width(3)) register_6 (.D(RtAdd), .en(En), .Q(RtAddEx), .clk(clk), .clr(clr));
  Register #(.width(16)) register_7 (.D(JumpAdd), .en(En), .Q(JumpAddEx), .clk(clk), .clr(clr));
  Register #(.width(16)) register_8 (.D(PCPlus4ID), .en(En), .Q(PCPlusEX), .clk(clk), .clr(clr));
  Register #(.width(1)) register_9 (.D(RegrtLID), .en(En), .Q(RegrtLEX), .clk(clk), .clr(clr));
  Register #(.width(1)) register_10 (.D(RegWrID), .en(En), .Q(RegWrEX), .clk(clk), .clr(clr));
  Register #(.width(1)) register_11 (.D(ExtOPID), .en(En), .Q(ExtOPEX), .clk(clk), .clr(clr));
  Register #(.width(1)) register_12 (.D(ALUSRCID), .en(En), .Q(ALUSRCEX), .clk(clk), .clr(clr));
  Register #(.width(1)) register_13 (.D(MemReadID), .en(En), .Q(MemReadEX), .clk(clk), .clr(clr));
  Register #(.width(1)) register_14 (.D(MemWriteID), .en(En), .Q(MemWriteEX), .clk(clk), .clr(clr));
  Register #(.width(1)) register_15 (.D(MemoryToRegID), .en(En), .Q(MemoryToRegEX), .clk(clk), .clr(clr));
  Register #(.width(1)) register_16 (.D(jID), .en(En), .Q(jEX), .clk(clk), .clr(clr));
  Register #(.width(1)) register_17 (.D(BranchID), .en(En), .Q(BranchEX), .clk(clk), .clr(clr));
endmodule

module EX_MEM (
  input  clk,
  input  clr,
  input  [15:0] ALUResultEX,
  input  MemtoRegEX,
  input  RegWriteEX,
  input  [15:0] RtEX,
  input  MemReadEX,
  input  MemWriteEX,
  input  [2:0] RdEX,
  input  En,
  output [15:0] ALUResultMEM,
  output MemtoRegMEM,
  output RegWriteMEM,
  output [15:0] RtMEM,
  output MemReadMEM,
  output jMEM,
  output [2:0] RdMEM
);

  Register #(.width(1)) register_1 (.D(MemtoRegEX), .en(En), .Q(MemtoRegMEM), .clk(clk), .clr(clr));
  Register #(.width(1)) register_2 (.D(RegWriteEX), .en(En), .Q(RegWriteMEM), .clk(clk), .clr(clr));
  Register #(.width(1)) register_3 (.D(MemReadEX), .en(En), .Q(MemReadMEM), .clk(clk), .clr(clr));
  Register #(.width(1)) register_4 (.D(MemWriteEX), .en(En), .Q(jMEM), .clk(clk), .clr(clr));
  Register #(.width(16)) register_5 (.D(ALUResultEX), .en(En), .Q(ALUResultMEM), .clk(clk), .clr(clr));
  Register #(.width(16)) register_6 (.D(RtEX), .en(En), .Q(RtMEM), .clk(clk), .clr(clr));
  Register #(.width(3)) register_7 (.D(RdEX), .en(En), .Q(RdMEM), .clk(clk), .clr(clr));
endmodule

// MEM/WBN
module MEM_WB (
  input  clk,
  input  clr,
  input  [15:0] ALUResultMEM,
  input  MemtoRegMEM,
  input  RegWriteMEM,
  input  [2:0] RdMEM,
  input  En,
  output [15:0] ALUResultWB,
  output MemtoRegWB,
  output RegWriteWB,
  output [2:0] RdWB
);

  Register #(.width(1)) register_1 (.D(MemtoRegMEM), .en(En), .Q(MemtoRegWB), .clk(clk), .clr(clr));
  Register #(.width(1)) register_2 (.D(RegWriteMEM), .en(En), .Q(RegWriteWB), .clk(clk), .clr(clr));
  Register #(.width(3)) register_3 (.D(RdMEM), .en(En), .Q(RdWB), .clk(clk), .clr(clr));
  Register #(.width(16)) register_4 (.D(ALUResultMEM), .en(En), .Q(ALUResultWB), .clk(clk), .clr(clr));
endmodule
