// Logisim project RegFile(3).circ as structural Verilog: 1 circuit, main circuit 8 bit register file
// 8 Bit register file
module _8_bit_register_file (
  input  [2:0] ReadReg1,
  input  [2:0] ReadReg2,
  input  [2:0] WriteReg,
  input  [15:0] WriteData,
  input  RegWr,
  input  CLK,
  input  [15:0] in_7,
  input  in_8,
  output [15:0] ReadData1,
  output [15:0] out_10
);

  wire and_1_out, and_2_out, and_3_out, and_4_out, and_5_out, and_6_out, and_7_out, and_8_out,
       decoder_1_out0, decoder_1_out1, decoder_1_out2, decoder_1_out3, decoder_1_out4, decoder_1_out5,
       decoder_1_out6, decoder_1_out7, not_1_out;
  wire [15:0] controlled_buffer_1_out, register_1_q, register_2_q, register_3_q, register_4_q, register_5_q,
       register_6_q, register_7_q, register_8_q;

  Decoder #(.select(3)) decoder_1 (
    .out0(decoder_1_out0), .out1(decoder_1_out1), .out2(decoder_1_out2), .out3(decoder_1_out3),
    .out4(decoder_1_out4), .out5(decoder_1_out5), .out6(decoder_1_out6), .out7(decoder_1_out7), .sel(WriteReg));  // open: en
  and and_1 (and_1_out, decoder_1_out0, 1'b0, RegWr);
  and and_2 (and_2_out, decoder_1_out1, RegWr);
  and and_3 (and_3_out, decoder_1_out2, RegWr);
  and and_4 (and_4_out, decoder_1_out3, RegWr);
  and and_5 (and_5_out, decoder_1_out4, RegWr);
  and and_6 (and_6_out, decoder_1_out5, RegWr);
  and and_7 (and_7_out, decoder_1_out6, RegWr);
  and and_8 (and_8_out, decoder_1_out7, RegWr);
  not not_1 (not_1_out, in_8);
  Register #(.width(16)) register_1 (.D(WriteData), .en(and_1_out), .Q(register_1_q), .clk(CLK));  // open: clr
  Register #(.width(16)) register_2 (.D(WriteData), .en(and_2_out), .Q(register_2_q), .clk(CLK));  // open: clr
  Register #(.width(16)) register_3 (.D(WriteData), .en(and_3_out), .Q(register_3_q), .clk(CLK));  // open: clr
  Register #(.width(16)) register_4 (.D(WriteData), .en(and_4_out), .Q(register_4_q), .clk(CLK));  // open: clr
  Register #(.width(16)) register_5 (.D(WriteData), .en(and_5_out), .Q(register_5_q), .clk(CLK));  // open: clr
  Register #(.width(16)) register_6 (.D(WriteData), .en(and_6_out), .Q(register_6_q), .clk(CLK));  // open: clr
  Register #(.width(16)) register_7 (.D(WriteData), .en(and_7_out), .Q(register_7_q), .clk(CLK));  // open: clr
  assign controlled_buffer_1_out = not_1_out ? WriteData : 16'bz;  // Controlled_Buffer controlled_buffer_1
  assign controlled_buffer_1_out = in_8 ? in_7 : 16'bz;  // Controlled_Buffer controlled_buffer_2
  Register #(.width(16)) register_8 (
    .D(controlled_buffer_1_out), .en(and_8_out), .Q(register_8_q), .clk(CLK));  // open: clr
  Multiplexer #(.select(3), .width(16)) multiplexer_1 (
    .in0(register_1_q), .in1(register_2_q), .in2(register_3_q), .in3(register_4_q), .in4(register_5_q),
    .in5(register_6_q), .in6(register_7_q), .in7(register_8_q), .out(ReadData1), .sel(ReadReg1));  // open: en
  Multiplexer #(.select(3), .width(16)) multiplexer_2 (
    .in0(register_1_q), .in1(register_2_q), .in2(register_3_q), .in3(register_4_q), .in4(register_5_q),
    .in5(register_6_q), .in6(register_7_q), .in7(register_8_q), .out(out_10), .sel(ReadReg2));  // open: en
endmodule
