// Logisim project SHift circut.circ as structural Verilog: 2 circuits, main circuit Shift
module Shift (
  input  in_1,
  input  in_2,
  input  in_3,
  input  in_4,
  input  in_5,
  input  in_6,
  input  [1:0] in_7,
  output X2,
  output X2_2,
  output X2_3,
  output X2_4
);

  wire button_1_out, CLK_out, multiplexer_1_out, multiplexer_2_out, multiplexer_3_out, multiplexer_4_out;

  Multiplexer #(.select(2)) multiplexer_1 (
    .in0(X2), .in1(in_1), .in2(X2_2), .in3(in_2), .out(multiplexer_1_out), .sel(in_7));  // open: en
  Multiplexer #(.select(2)) multiplexer_2 (
    .in0(X2_2), .in1(X2), .in2(X2_3), .in3(in_3), .out(multiplexer_2_out), .sel(in_7));  // open: en
  Multiplexer #(.select(2)) multiplexer_3 (
    .in0(X2_3), .in1(X2_2), .in2(X2_4), .in3(in_4), .out(multiplexer_3_out), .sel(in_7));  // open: en
  Multiplexer #(.select(2)) multiplexer_4 (
    .in0(X2_4), .in1(X2_3), .in2(in_6), .in3(in_5), .out(multiplexer_4_out), .sel(in_7));  // open: en
  D_Flip_Flop d_ff_1 (.clk(CLK_out), .D(multiplexer_1_out), .Q(X2), .reset(button_1_out));  // open: Qn, preset, en
  D_Flip_Flop d_ff_2 (.clk(CLK_out), .D(multiplexer_2_out), .Q(X2_2), .reset(button_1_out));  // open: Qn, preset, en
  D_Flip_Flop d_ff_3 (.clk(CLK_out), .D(multiplexer_3_out), .Q(X2_3), .reset(button_1_out));  // open: Qn, preset, en
  D_Flip_Flop d_ff_4 (.clk(CLK_out), .D(multiplexer_4_out), .Q(X2_4), .reset(button_1_out));  // open: Qn, preset, en
  Clock CLK (.out(CLK_out));
  Button button_1 (.out(button_1_out));
endmodule

module shift (
  input  [15:0] in_1,
  input  [15:0] in_2,
  input  in_3,
  input  in_4,
  input  in_5,
  output [15:0] X2
);

  wire decoder_1_out4, decoder_1_out5, decoder_1_out6, decoder_1_out7;
  wire [3:0] bit_extender_1_out;
  wire [15:0] shifter_1_out, shifter_2_out, shifter_3_out, shifter_4_out;

  Decoder #(.select(3)) decoder_1 (
    .out4(decoder_1_out4), .out5(decoder_1_out5), .out6(decoder_1_out6), .out7(decoder_1_out7),
    .sel({in_3, in_4, in_5}));  // open: out0, out1, out2, out3, en
  Bit_Extender #(.in_width(16), .out_width(4)) bit_extender_1 (.in(in_2), .out(bit_extender_1_out));
  Shifter #(.width(16)) shifter_1 (.in(in_1), .\dist (bit_extender_1_out), .out(shifter_1_out));
  Shifter #(.width(16), .shift("lr")) shifter_2 (.in(in_1), .\dist (bit_extender_1_out), .out(shifter_2_out));
  assign X2 = decoder_1_out5 ? shifter_2_out : 16'bz;  // Controlled_Buffer controlled_buffer_1
  assign X2 = decoder_1_out4 ? shifter_1_out : 16'bz;  // Controlled_Buffer controlled_buffer_2
  assign X2 = decoder_1_out6 ? shifter_3_out : 16'bz;  // Controlled_Buffer controlled_buffer_3
  Shifter #(.width(16), .shift("ar")) shifter_3 (.in(in_1), .\dist (bit_extender_1_out), .out(shifter_3_out));
  assign X2 = decoder_1_out7 ? shifter_4_out : 16'bz;  // Controlled_Buffer controlled_buffer_4
  Shifter #(.width(16), .shift("rl")) shifter_4 (.in(in_1), .\dist (bit_extender_1_out), .out(shifter_4_out));
endmodule
