// Logisim project Single cycle(1).circ as structural Verilog
module Single_Cycle (
  input  in_1
);

  wire ALUSRC, ALUSRCEX, and_1_out, BGEZ, BGT, BGTZ, BLEZ, BLT, BLTZ, BNEQ, Branch, Branch_Hazard, BranchEX,
       CLock, control_branch_1_one, ExtOP, ExtOPEX, i_tpye_1_o1, i_tpye_1_o2, i_tpye_1_o3, i_tpye_1_o4, j,
       jEX, JR, JR_ON, JRAL, JRCheck, JumpBubbel, LINK, Load_detect, Lui_On, MemoryToReg, MemoryToRegEX,
       MemoryToRegMEM, MemoryToRegWB, MemRead, MemReadEX, MemReadMEM, MemWrite, MemWriteEX, MemWriteMEM,
       multiplexer_5_out, multiplexer_10_out, multiplexer_11_out, multiplexer_12_out, multiplexer_13_out,
       multiplexer_14_out, multiplexer_15_out, multiplexer_16_out, not_1_out, not_2_out, not_3_out, or_1_out,
       or_2_out, or_3_out, or_4_out, Regrt, RegrtEX, RegWr, RegWrEX, RegWrMEM, RegWrWB, ZeroFlag;
  wire [1:0] Forward;
  wire [2:0] JREG, multiplexer_6_out, Rd, RdEX, RdMEM, RdWB, RsAddEx, RtAddtEX;
  wire [11:0] _12imm, _12immEX;
  wire [15:0] _12immExtend, adder_2_out, adder_3_out, alu_0001_1_out_6, ALUResEX, ALUResultMEM, ALUResultWB,
       bit_extender_1_out, bit_extender_2_out, bit_extender_3_out, bit_extender_4_out, Bus_Rs, Bus_Rs_EX,
       Bus_Rt, Bus_Rt_EX, Bus_Rt_MEM, controlled_buffer_1_out, controlled_buffer_3_out,
       controlled_buffer_5_out, i_type_1_out_7, InstructionID, JAL, jumpAdd, jumpAddEX, Lui, main_1_out_6,
       multiplexer_1_out, multiplexer_4_out, multiplexer_8_out, multiplexer_9_out, multiplexer_17_out,
       multiplexer_18_out, multiplexer_21_out, Pc, Pc_1, PcEX, PcID, ram_1_data, register_1_q;
  wire [15:12] Instruction;

  control_branch control_branch_1 (
    .op1(Instruction[15]), .op2(Instruction[14]), .op3(Instruction[13]), .op4(Instruction[12]),
    .one(control_branch_1_one));
  and and_1 (and_1_out, control_branch_1_one, BGT);
  Adder #(.width(16)) adder_1 (.a(Pc), .b(16'h1), .out(Pc_1));  // open: cin, cout
  and and_2 (Branch_Hazard, Branch, ZeroFlag);
  Clock clock_1 (.out(CLock));
  Multiplexer #(.width(16), .enable("false")) multiplexer_1 (
    .in0(controlled_buffer_1_out), .in1(Pc_1), .out(multiplexer_1_out), .sel(Load_detect));
  assign controlled_buffer_1_out = Branch_Hazard ? adder_3_out : 16'bz;  // Controlled_Buffer controlled_buffer_1
  not not_1 (not_1_out, Branch_Hazard);
  Register #(.width(16)) register_1 (.D(multiplexer_1_out), .Q(register_1_q), .clk(CLock), .clr(in_1));  // open: en
  Multiplexer #(.width(16), .enable("false")) multiplexer_2 (
    .in0(register_1_q), .in1(PcID), .out(Pc), .sel(Load_detect));
  assign controlled_buffer_1_out = not_1_out ? jumpAdd : 16'bz;  // Controlled_Buffer controlled_buffer_2
  assign bit_extender_1_out = {{10{_12imm[5]}}, _12imm[5:0]};  // Bit_Extender bit_extender_1
  Multiplexer #(.width(16), .enable("false")) multiplexer_3 (
    .in0(adder_2_out), .in1(controlled_buffer_3_out), .out(jumpAdd), .sel(or_1_out));
  Adder #(.width(16)) adder_2 (.a(register_1_q), .b(16'h1), .out(adder_2_out));  // open: cin, cout
  Adder #(.width(16)) adder_3 (.a(adder_2_out), .b(bit_extender_1_out), .out(adder_3_out));  // open: cin, cout
  assign controlled_buffer_3_out = JumpBubbel ? multiplexer_4_out : 16'bz;  // Controlled_Buffer controlled_buffer_3
  or or_1 (or_1_out, JRAL, JR_ON, JumpBubbel);
  Adder #(.width(16)) adder_4 (.a(register_1_q), .b(16'h1), .out(JAL));  // open: cin, cout
  ROM #(.addrWidth(16), .dataWidth(16)) rom_1 (.addr(Pc), .data({Instruction, _12imm}));  // open: sel
  assign controlled_buffer_3_out = JR_ON ? bit_extender_3_out : 16'bz;  // Controlled_Buffer controlled_buffer_4
  Multiplexer #(.width(16), .enable("false")) multiplexer_4 (
    .in0(_12immExtend), .in1(bit_extender_2_out), .out(multiplexer_4_out), .sel(JR_ON));
  and and_3 (LINK, Instruction[15], not_2_out, Instruction[13], Instruction[12]);
  assign bit_extender_2_out = {{4{1'b0}}, Bus_Rs[11:0]};  // Bit_Extender bit_extender_2
  and and_4 (JumpBubbel, j, ~Branch_Hazard);  // AND_Gate
  not not_2 (not_2_out, Instruction[14]);
  or or_2 (or_2_out, JumpBubbel, Branch_Hazard);
  OP_0000_0001 op_0000_0001_1 (
    .OP1(Instruction[15]), .OP2(Instruction[14]), .OP3(Instruction[13]), .OP4(Instruction[12]), .ONE(JRCheck));
  IF_ID if_id_1 (
    .InstIF({Instruction, _12imm}), .InstID(InstructionID), .clk(CLock), .En(multiplexer_5_out),
    .clr(or_2_out), .PCPlus4ID(Pc), .PCPlus4IF(PcID));
  Multiplexer #(.enable("false")) multiplexer_5 (.in0(1'b1), .in1(1'b0), .out(multiplexer_5_out), .sel(Load_detect));
  and and_5 (JR_ON, JRCheck, JR);
  assign bit_extender_3_out = {{4{1'b0}}, Bus_Rs[11:0]};  // Bit_Extender bit_extender_3
  Selcet_Lui selcet_lui_1 (
    .op0(Instruction[15]), .op1(Instruction[14]), .one(Lui_On), .op2(Instruction[13]), .op3(Instruction[12]));  // open: zero
  Shifter #(.width(16)) shifter_1 (.in({Instruction, _12imm}), .\dist (4'b1000), .out(Lui));
  Multiplexer #(.width(3), .enable("false")) multiplexer_6 (
    .in0(_12imm[8:6]), .in1(_12imm[5:3]), .out(multiplexer_6_out), .sel(Regrt));
  or or_3 (or_3_out, Lui_On, LINK);
  Load_delay_detect load_delay_detect_1 (.out_3(Load_detect), ._1__Forward(Forward), .EX_MemRd(MemReadEX));
  Multiplexer #(.width(3), .enable("false")) multiplexer_7 (
    .in0(multiplexer_6_out), .in1(JREG), .out(Rd), .sel(or_3_out));
  Forward_unit__Branch forward_unit_branch_1 (
    .RS_EX(RsAddEx), .RT_EX(RtAddtEX), .RD_WB(RdWB), .forward_S(Forward), .RD_MEM(RdMEM));
  or or_4 (or_4_out, Branch_Hazard, Load_detect);
  Multiplexer #(.width(16), .enable("false")) multiplexer_8 (
    .in0(multiplexer_21_out), .in1(multiplexer_9_out), .out(multiplexer_8_out), .sel(or_3_out));
  assign bit_extender_4_out = {{10{_12imm[5]}}, _12imm[5:0]};  // Bit_Extender bit_extender_4
  _16_Bit_Register u_16_bit_register_1 (
    .Read_Register_1(_12imm[11:9]), .Read_Register_2(_12imm[8:6]), .Write_Register(Rd),
    .Write_Data(multiplexer_8_out), .Data_1(Bus_Rs), .Data_2(Bus_Rt), .regWrite(RegWr), .Clock(CLock));
  Multiplexer #(.width(16)) multiplexer_9 (.in0(Lui), .in1(Pc_1), .out(multiplexer_9_out), .sel(LINK));  // open: en
  Multiplexer #(.enable("false")) multiplexer_10 (.in0(Regrt), .in1(1'b0), .out(multiplexer_10_out), .sel(or_4_out));
  Multiplexer #(.enable("false")) multiplexer_11 (.in0(ALUSRC), .in1(1'b0), .out(multiplexer_11_out), .sel(or_4_out));
  Multiplexer #(.enable("false")) multiplexer_12 (.in0(ExtOP), .in1(1'b0), .out(multiplexer_12_out), .sel(or_4_out));
  Multiplexer #(.enable("false")) multiplexer_13 (
    .in0(MemoryToReg), .in1(1'b0), .out(multiplexer_13_out), .sel(or_4_out));
  Multiplexer #(.enable("false")) multiplexer_14 (.in0(Branch), .in1(1'b0), .out(multiplexer_14_out), .sel(or_4_out));
  Multiplexer #(.enable("false")) multiplexer_15 (.in0(j), .in1(1'b0), .out(multiplexer_15_out), .sel(or_4_out));
  Multiplexer #(.enable("false")) multiplexer_16 (.in0(MemRead), .in1(1'b0), .out(multiplexer_16_out), .sel(or_4_out));
  Multiplexer #(.select(2), .width(16)) multiplexer_17 (
    .in0(Bus_Rs), .in1(ALUResEX), .in2(ALUResultWB), .out(multiplexer_17_out), .sel(Forward));  // open: in3, en
  Multiplexer #(.select(2), .width(16)) multiplexer_18 (
    .in0(Bus_Rt), .in1(ALUResEX), .in2(ALUResultWB), .out(multiplexer_18_out), .sel(Forward));  // open: in3, en
  Control_Unit control_unit_1 (
    .op1(Instruction[15]), .op2(Instruction[14]), .op3(Instruction[13]), .op4(Instruction[12]),
    .RegDis(Regrt), .RegWr(RegWr), .Extop(ExtOP), .AluSrc(ALUSRC), .MemRd(MemRead), .MemWr(MemWrite),
    .MemToReg(MemoryToReg), .Jump(j), .Branch(Branch));
  ID_EX id_ex_1 (
    .clk(CLock), .RegrtLID(multiplexer_10_out), .jID(multiplexer_15_out), .RegWrID(RegWr),
    .BranchID(multiplexer_14_out), .ExtOPID(multiplexer_12_out), .ALUSRCID(multiplexer_11_out),
    .MemReadID(multiplexer_16_out), .MemWriteID(MemWrite), .MemoryToRegID(multiplexer_13_out),
    .RegrtLEX(RegrtEX), .jEX(jEX), .RegWrEX(RegWrEX), .BranchEX(BranchEX), .ExtOPEX(ExtOPEX),
    .ALUSRCEX(ALUSRCEX), .MemReadEX(MemReadEX), .MemWriteEX(MemWriteEX), .MemoryToRegEX(MemoryToRegEX),
    .ImmID(_12imm), .ImmEX(_12immEX), .R1ID(multiplexer_17_out), .R1EX(Bus_Rs_EX), .R2ID(multiplexer_18_out),
    .R2EX(Bus_Rt_EX), .JumpAdd(jumpAdd), .JumpAddEx(jumpAddEX), .RtAdd(_12imm[8:6]), .RtAddEx(RtAddtEX),
    .En(1'b1), .RdID(Rd), .RdEX(RdEX), .RsAdd(_12imm[11:9]), .RsAddEx(RsAddEx), .PCPlus4ID(PcID),
    .PCPlusEX(PcEX));  // open: clr
  assign _12immExtend = {{4{1'b0}}, _12imm};  // Bit_Extender bit_extender_5
  Multiplexer #(.width(3)) multiplexer_19 (.in0(3'b001), .in1(3'b111), .out(JREG), .sel(LINK));  // open: en
  i_TPYE i_tpye_1 (
    .OP1(Instruction[15]), .OP2(Instruction[14]), .OP3(Instruction[13]), .OP4(Instruction[12]),
    .O1(i_tpye_1_o1), .O2(i_tpye_1_o2), .O3(i_tpye_1_o3), .O4(i_tpye_1_o4));
  _16_bit_main main_1 (
    .in_4(Bus_Rs), .in_5(Bus_Rt), .out_6(main_1_out_6), .in_1(_12imm[2]), .in_2(_12imm[1]), .in_3(_12imm[0]));
  I_Type i_type_1 (
    .in_1(Bus_Rs), .in_2(bit_extender_4_out), .out_7(i_type_1_out_7), .in_3(i_tpye_1_o1), .in_4(i_tpye_1_o2),
    .in_5(i_tpye_1_o3), .in_6(i_tpye_1_o4));
  Alu_0001 alu_0001_1 (
    .in_1(Bus_Rs), .in_2(Bus_Rt), .out_6(alu_0001_1_out_6), .in_3(_12imm[2]), .in_4(_12imm[1]),
    .in_5(_12imm[0]), .out_7(JR), .out_8(JRAL));
  assign controlled_buffer_5_out = Instruction[12] ? alu_0001_1_out_6 : 16'bz;  // Controlled_Buffer controlled_buffer_5
  not not_3 (not_3_out, Instruction[12]);
  assign controlled_buffer_5_out = not_3_out ? main_1_out_6 : 16'bz;  // Controlled_Buffer controlled_buffer_6
  Branch_main main_2 (
    .Zero_flag(ZeroFlag), .BLT(BLT), .BGT(BGT), .BGTZ(BGTZ), .BLTZ(BLTZ), .BGEZ(BGEZ), .BLEZ(BLEZ),
    .in_1(Bus_Rs), .in_2(Bus_Rt), .BEQ(BNEQ));
  EX_MEM ex_mem_1 (
    .MemReadEX(MemReadEX), .MemReadMEM(MemReadMEM), .MemWriteEX(MemWriteEX), .jMEM(MemWriteMEM),
    .RegWriteEX(RegWrEX), .RegWriteMEM(RegWrMEM), .MemtoRegEX(MemoryToRegEX), .MemtoRegMEM(MemoryToRegMEM),
    .clk(CLock), .ALUResultEX(ALUResEX), .ALUResultMEM(ALUResultMEM), .En(1'b1), .RdEX(RdEX), .RdMEM(RdMEM),
    .RtEX(Bus_Rt_EX), .RtMEM(Bus_Rt_MEM));  // open: clr
  Multiplexer #(.width(16)) multiplexer_20 (
    .in0(controlled_buffer_5_out), .in1(i_type_1_out_7), .out(ALUResEX), .sel(ALUSRC));  // open: en
  RAM #(.addrWidth(16), .dataWidth(16), .bus("separate")) ram_1 (
    .addr(ALUResEX), .din(Bus_Rt), .data(ram_1_data), .str(MemWrite), .clk(CLock), .ld(MemRead));  // open: sel, clr
  MEM_WB mem_wb_1 (
    .clk(CLock), .MemtoRegMEM(MemoryToRegMEM), .RegWriteMEM(RegWrMEM), .MemtoRegWB(MemoryToRegWB),
    .RegWriteWB(RegWrWB), .ALUResultMEM(ALUResultMEM), .ALUResultWB(ALUResultWB), .RdMEM(RdMEM), .RdWB(RdWB),
    .En(1'b1));  // open: clr
  Multiplexer #(.width(16)) multiplexer_21 (
    .in0(ALUResEX), .in1(ram_1_data), .out(multiplexer_21_out), .sel(MemoryToReg));  // open: en

  // Other names for the same wires on the sheet: f0 = _12imm[0]; Instruction[11:0] = _12imm;
  //   Pc_Branch[5:0] = _12imm[5:0]; f1 = _12imm[1]; f2 = _12imm[2]; Rt[2:0] = _12imm[8:6]; Rs[2:0] = _12imm[11:9];
  //   JrPC[11:0] = Bus_Rs[11:0]; OP4 = Instruction[12]; OP3 = Instruction[13]; OP2 = Instruction[14];
  //   OP1 = Instruction[15]; Kill_2 = Branch_Hazard

  // Notes on the sheet:
  //   contents of rom_1 (hex, n*v repeats v):
  //   a384 8354 35b 2040 2081 20c2 890a 1921 1520 14f2 4c02 1290 403b 3100 b012 55c 1b68 403f 4e9 2040
  //   2285 22c6 4e0 3100 1e06
  //   JR Control
  //   Lui Control
  //   Load Detect
  //   Control Forwarding
  //   Control Unit
endmodule

module i_TPYE (
  input  OP1,
  input  OP2,
  input  OP3,
  input  OP4,
  output O1,
  output O2,
  output O3,
  output O4
);

  not not_1 (O1, OP2);
  and and_1 (O4, OP2, OP4);

  assign O2 = OP2;
  assign O3 = OP2;
endmodule

module Selcet_Lui (
  input  op0,
  input  op1,
  input  op2,
  input  op3,
  output zero,
  output one
);

  wire not_1_out, not_2_out;

  not not_1 (not_1_out, op1);
  not not_2 (not_2_out, op3);
  and and_1 (one, op0, not_1_out, op2, not_2_out);

  assign zero = 1'b0;
endmodule

module SELECT_JAL (
  input  OP1,
  input  OP2,
  input  OP3,
  input  OP4,
  output ONE,
  output ZERO
);

  wire not_1_out;

  not not_1 (not_1_out, OP2);
  and and_1 (ONE, OP1, not_1_out, OP3, OP4);

  assign ZERO = 1'b0;
endmodule

module OP_0000_0001 (
  input  OP1,
  input  OP2,
  input  OP3,
  input  OP4,
  output ONE
);

  wire not_1_out, not_2_out, not_3_out;

  not not_1 (not_1_out, OP1);
  not not_2 (not_2_out, OP2);
  and and_1 (ONE, not_1_out, not_2_out, not_3_out);
  not not_3 (not_3_out, OP3);
endmodule

module Load_delay_detect (
  input  [1:0] _1__Forward,
  input  EX_MemRd,
  output out_3
);

  wire not_1_out;

  not not_1 (not_1_out, _1__Forward[1]);
  and and_1 (out_3, _1__Forward[0], not_1_out, EX_MemRd);
endmodule

module Control_Unit (
  input  op1,
  input  op2,
  input  op3,
  input  op4,
  output RegDis,
  output RegWr,
  output Extop,
  output AluSrc,
  output MemRd,
  output MemWr,
  output MemToReg,
  output Jump,
  output Branch
);

  wire and_1_out, and_2_out, and_3_out, and_4_out, and_5_out, and_6_out, and_7_out, and_8_out, and_9_out,
       and_10_out, and_11_out, and_13_out, and_14_out, and_17_out, and_18_out, not_1_out, not_2_out,
       not_3_out, not_4_out, not_5_out, not_6_out, not_7_out, not_8_out, not_9_out, not_10_out, not_11_out,
       not_12_out, not_13_out, not_14_out, not_15_out, not_16_out, not_17_out, not_18_out, not_19_out,
       not_20_out, not_21_out, not_22_out, not_23_out, not_24_out, not_25_out, not_26_out, not_27_out;

  not not_1 (not_1_out, op1);
  and and_1 (and_1_out, not_1_out, not_2_out);
  not not_2 (not_2_out, op3);
  and and_2 (and_2_out, op1, op3, op4);
  not not_3 (not_3_out, op1);
  and and_3 (and_3_out, not_3_out, not_4_out, not_5_out);
  not not_4 (not_4_out, op2);
  not not_5 (not_5_out, op3);
  not not_6 (not_6_out, op2);
  and and_4 (and_4_out, not_6_out, not_7_out);
  not not_7 (not_7_out, op4);
  not not_8 (not_8_out, op1);
  and and_5 (and_5_out, not_8_out, op2, op3);
  not not_9 (not_9_out, op2);
  and and_6 (and_6_out, op1, not_9_out, op3);
  not not_10 (not_10_out, op2);
  and and_7 (and_7_out, not_10_out, not_11_out);
  not not_11 (not_11_out, op4);
  not not_12 (not_12_out, op2);
  and and_8 (and_8_out, not_12_out, op3);
  and and_9 (and_9_out, op2, not_13_out);
  not not_13 (not_13_out, op3);
  not not_14 (not_14_out, op1);
  and and_10 (and_10_out, not_14_out, op3);
  not not_15 (not_15_out, op2);
  and and_11 (and_11_out, op1, not_15_out, not_16_out);
  not not_16 (not_16_out, op4);
  not not_17 (not_17_out, op1);
  not not_18 (not_18_out, op2);
  not not_19 (not_19_out, op4);
  not not_20 (not_20_out, op1);
  not not_21 (not_21_out, op2);
  not not_22 (not_22_out, op1);
  not not_23 (not_23_out, op2);
  not not_24 (not_24_out, op4);
  not not_25 (not_25_out, op2);
  not not_26 (not_26_out, op2);
  and and_12 (Jump, op1, not_26_out, op4);
  and and_13 (and_13_out, op2, not_27_out);
  not not_27 (not_27_out, op3);
  and and_14 (and_14_out, op1, op2);
  or or_1 (RegDis, and_1_out, and_2_out);
  or or_2 (RegWr, and_3_out, and_4_out, and_5_out, and_6_out);
  or or_3 (Extop, and_7_out, and_8_out, and_9_out, op1);
  or or_4 (AluSrc, and_10_out, and_11_out);
  and and_15 (MemRd, not_17_out, not_18_out, op3, not_19_out);
  and and_16 (MemWr, not_20_out, not_21_out, op3, op4);
  and and_17 (and_17_out, not_22_out, not_23_out, op3, not_24_out);
  or or_5 (MemToReg, and_17_out, and_18_out);
  and and_18 (and_18_out, op1, not_25_out, op3, op4);
  or or_6 (Branch, and_13_out, and_14_out);
endmodule

module Control_Unit1 (
  input  op1,
  input  op2,
  input  op3,
  input  op4,
  output RegDis,
  output RegWr,
  output Extop,
  output AluSrc,
  output MemRd,
  output MemWr,
  output MemToReg,
  output Jump,
  output Branch
);

  wire and_1_out, and_2_out, and_3_out, and_4_out, and_5_out, and_6_out, and_7_out, and_8_out, and_9_out,
       and_10_out, and_11_out, and_13_out, and_14_out, and_17_out, and_18_out, not_1_out, not_2_out,
       not_3_out, not_4_out, not_5_out, not_6_out, not_7_out, not_8_out, not_9_out, not_10_out, not_11_out,
       not_12_out, not_13_out, not_14_out, not_15_out, not_16_out, not_17_out, not_18_out, not_19_out,
       not_20_out, not_21_out, not_22_out, not_23_out, not_24_out, not_25_out, not_26_out, not_27_out;

  not not_1 (not_1_out, op1);
  and and_1 (and_1_out, not_1_out, not_2_out);
  not not_2 (not_2_out, op3);
  and and_2 (and_2_out, op1, op3, op4);
  not not_3 (not_3_out, op1);
  and and_3 (and_3_out, not_3_out, not_4_out, not_5_out);
  not not_4 (not_4_out, op2);
  not not_5 (not_5_out, op3);
  not not_6 (not_6_out, op2);
  and and_4 (and_4_out, not_6_out, not_7_out);
  not not_7 (not_7_out, op4);
  not not_8 (not_8_out, op1);
  and and_5 (and_5_out, not_8_out, op2, op3);
  not not_9 (not_9_out, op2);
  and and_6 (and_6_out, op1, not_9_out, op3);
  not not_10 (not_10_out, op2);
  and and_7 (and_7_out, not_10_out, not_11_out);
  not not_11 (not_11_out, op4);
  not not_12 (not_12_out, op2);
  and and_8 (and_8_out, not_12_out, op3);
  and and_9 (and_9_out, op2, not_13_out);
  not not_13 (not_13_out, op3);
  not not_14 (not_14_out, op1);
  and and_10 (and_10_out, not_14_out, op3);
  and and_11 (and_11_out, op1, not_15_out, not_16_out);
  not not_15 (not_15_out, op2);
  not not_16 (not_16_out, op4);
  not not_17 (not_17_out, op1);
  not not_18 (not_18_out, op2);
  not not_19 (not_19_out, op4);
  not not_20 (not_20_out, op1);
  not not_21 (not_21_out, op2);
  not not_22 (not_22_out, op1);
  not not_23 (not_23_out, op2);
  not not_24 (not_24_out, op4);
  not not_25 (not_25_out, op2);
  and and_12 (Jump, op1, not_26_out, op4);
  not not_26 (not_26_out, op2);
  and and_13 (and_13_out, op2, not_27_out);
  not not_27 (not_27_out, op3);
  and and_14 (and_14_out, op1, op2);
  or or_1 (RegDis, and_1_out, and_2_out);
  or or_2 (RegWr, and_3_out, and_4_out, and_5_out, and_6_out);
  or or_3 (Extop, and_7_out, and_8_out, and_9_out, op1);
  or or_4 (AluSrc, and_10_out, and_11_out);
  and and_15 (MemRd, not_17_out, not_18_out, op3, not_19_out);
  and and_16 (MemWr, not_20_out, not_21_out, op3, op4);
  and and_17 (and_17_out, not_22_out, not_23_out, op3, not_24_out);
  or or_5 (MemToReg, and_17_out, and_18_out);
  and and_18 (and_18_out, op1, not_25_out, op3, op4);
  or or_6 (Branch, and_13_out, and_14_out);
endmodule

module control_branch (
  input  op1,
  input  op2,
  input  op3,
  input  op4,
  output one
);

  wire and_1_out, and_2_out, not_1_out;

  and and_1 (and_1_out, op2, not_1_out);
  not not_1 (not_1_out, op3);
  and and_2 (and_2_out, op1, op2);
  or or_1 (one, and_1_out, and_2_out);
endmodule
