// Logisim project forward unit.circ as structural Verilog: 1 circuit, main circuit Forward unit (Branch)
module Forward_unit__Branch (
  input  [2:0] RD_MEM,
  input  [2:0] RS_EX,
  input  [2:0] RT_EX,
  input  [2:0] RD_WB,
  output [1:0] forward_S
);

  wire comparator_1_eq, comparator_2_eq, comparator_3_eq, comparator_4_eq;
  wire [1:0] or_1_out;

  Comparator #(.width(3)) comparator_1 (.a(RD_MEM), .b(RS_EX), .eq(comparator_1_eq));  // open: gt, lt
  Comparator #(.width(3)) comparator_2 (.a(RD_MEM), .b(RT_EX), .eq(comparator_2_eq));  // open: gt, lt
  Comparator #(.width(3)) comparator_3 (.a(RD_WB), .b(RS_EX), .eq(comparator_3_eq));  // open: gt, lt
  Comparator #(.width(3)) comparator_4 (.a(RD_WB), .b(RT_EX), .eq(comparator_4_eq));  // open: gt, lt
  or or_1 (or_1_out[0], comparator_1_eq, comparator_2_eq);
  or or_2 (or_1_out[1], comparator_3_eq, comparator_4_eq);
  Multiplexer #(.select(2), .width(2), .enable("false")) multiplexer_1 (
    .in0(2'b00), .in1(2'b01), .in2(2'b10), .in3(2'b11), .out(forward_S), .sel(or_1_out));
endmodule
